// Logisim project Aniol64keyboard.circ as structural Verilog: 1 circuit, main circuit main
module main (
  input  in_1,
  input  IEI,
  input  in_3,
  output IEO,
  output INT
);

  wire and_1_out, CLK, d_ff_1_q, d_ff_1_qn, demultiplexer_1_out0, demultiplexer_1_out3, or_1_out,
       pull_resistor_1_node, switch_1_p1, switch_1_p5, switch_1_p6;
  wire [6:0] counter_1_q;

  Clock clock_1 (.out(CLK));
  Pull_Resistor pull_resistor_1 (.node(pull_resistor_1_node));
  Counter #(.max('h7f), .width(7)) counter_1 (
    .clr(in_1), .clk(or_1_out), .Q(counter_1_q));  // open: load, up, count, D, carry
  or or_1 (or_1_out, CLK, pull_resistor_1_node);
  Register #(.width(7)) register_1 (.D(counter_1_q), .clk(and_1_out));  // open: en, Q, clr
  LED led_1 (.in(pull_resistor_1_node));
  Multiplexer #(.enable("false"), .select(3)) multiplexer_1 (
    .in2(switch_1_p5), .out(pull_resistor_1_node), .sel(counter_1_q[6:4]));  // open: in0, in1, in3, in4, in5, in6, in7
  D_Flip_Flop d_ff_1 (
    .D(1'b1), .clk(pull_resistor_1_node), .Q(d_ff_1_q), .Qn(d_ff_1_qn), .reset(in_3));  // open: preset
  and and_1 (and_1_out, d_ff_1_q, IEI);
  Demultiplexer #(.enable("false"), .select(4)) demultiplexer_1 (
    .out0(demultiplexer_1_out0), .out3(demultiplexer_1_out3), .in(1'b1), .sel(counter_1_q[3:0]));  // open: out1, out2, out4, out5, out6, out7, out8, out9, out10, out11, out12, out13, out14, out15
  // Switch switch_1: pin names not known; wires that end beside it: switch_1_p1, demultiplexer_1_out0, switch_1_p1, demultiplexer_1_out3, switch_1_p5, switch_1_p6, switch_1_p6
  not not_1 (INT, and_1_out);
  and and_2 (IEO, IEI, d_ff_1_qn);

  // Notes on the sheet:
  //   Interrupt Acknowledge
endmodule
